// Digital circuit ALU.dig as structural Verilog
module ALU (
  input  [2:0] Op,
  input  [7:0] A,
  input  [7:0] B,
  output OF,
  output eq,
  output lt,
  output gt,
  output [7:0] R
);

  wire decoder_1_out_0, decoder_1_out_1, decoder_1_out_2, decoder_1_out_3, decoder_1_out_4, decoder_1_out_5,
       decoder_1_out_6, decoder_1_out_7, fulladder16_1_cout, multiplicador_1_cout, subtrator8_1_cout;
  wire [7:0] fulladder16_1_soma, leftshift_1_als, multiplicador_1_r, seletor8bit_1_ns, seletor8bit_2_ns,
       seletor8bit_3_ns, seletor8bit_4_ns, seletor8bit_5_ns, seletor8bit_6_ns, seletor8bit_7_ns,
       seletor8bit_8_ns, seletor8bit_9_ns, subtrator8_1_diff;

  Decoder #(.Selector_Bits(3)) decoder_1 (
    .sel(Op), .out_0(decoder_1_out_0), .out_1(decoder_1_out_1), .out_2(decoder_1_out_2),
    .out_3(decoder_1_out_3), .out_4(decoder_1_out_4), .out_5(decoder_1_out_5), .out_6(decoder_1_out_6),
    .out_7(decoder_1_out_7));
  LED led_1 (.in(decoder_1_out_5));
  LED led_2 (.in(decoder_1_out_6));
  LED led_3 (.in(decoder_1_out_7));
  seletor8bit seletor8bit_1 (.N(A), .S(decoder_1_out_0), .NS(seletor8bit_1_ns));
  seletor8bit seletor8bit_2 (.N(B), .S(decoder_1_out_0), .NS(seletor8bit_2_ns));
  seletor8bit seletor8bit_3 (.N(A), .S(decoder_1_out_1), .NS(seletor8bit_3_ns));
  seletor8bit seletor8bit_4 (.N(B), .S(decoder_1_out_1), .NS(seletor8bit_4_ns));
  seletor8bit seletor8bit_5 (.N(A), .S(decoder_1_out_2), .NS(seletor8bit_5_ns));
  seletor8bit seletor8bit_6 (.N(B), .S(decoder_1_out_2), .NS(seletor8bit_6_ns));
  seletor8bit seletor8bit_7 (.N(A), .S(decoder_1_out_3), .NS(seletor8bit_7_ns));
  seletor8bit seletor8bit_8 (.N(A), .S(decoder_1_out_4), .NS(seletor8bit_8_ns));
  seletor8bit seletor8bit_9 (.N(B), .S(decoder_1_out_4), .NS(seletor8bit_9_ns));
  multiplicador multiplicador_1 (
    .A(seletor8bit_1_ns[3:0]), .B(seletor8bit_2_ns[3:0]), .R(multiplicador_1_r), .Cout(multiplicador_1_cout));
  subtrator8 subtrator8_1 (
    .B(seletor8bit_4_ns), .A(seletor8bit_3_ns), .Cout(subtrator8_1_cout), .Diff(subtrator8_1_diff));
  fullAdder16 fulladder16_1 (
    .A(seletor8bit_5_ns), .B(seletor8bit_6_ns), .Cin(1'b0), .Cout(fulladder16_1_cout),
    .Soma(fulladder16_1_soma));
  leftShift leftshift_1 (.A(seletor8bit_7_ns), .ALs(leftshift_1_als));
  comparador comparador_1 (.A(seletor8bit_8_ns), .B(seletor8bit_9_ns), .eq(eq), .lt(lt), .gt(gt));
  xor xor_1 (OF, subtrator8_1_cout, fulladder16_1_cout, multiplicador_1_cout, 1'b0);
  Multiplexer #(.Selector_Bits(3), .Bits(8)) multiplexer_1 (
    .sel(Op), .in_0(multiplicador_1_r), .in_1(subtrator8_1_diff), .in_2(fulladder16_1_soma),
    .in_3(leftshift_1_als), .in_4({8{1'b0}}), .in_5({8{1'b0}}), .in_6({8{1'b0}}), .in_7({8{1'b0}}), .out(R));
  // also tied to GND on the sheet: {seletor8bit_1_ns[4], seletor8bit_1_ns[5], seletor8bit_1_ns[6], seletor8bit_1_ns[7], seletor8bit_2_ns[4], seletor8bit_2_ns[5], seletor8bit_2_ns[6], seletor8bit_2_ns[7]}
endmodule
