// Digital circuit DisplayAl.dig as structural Verilog
module DisplayAl (
  input  [2:0] in_1,
  input  [7:0] A,
  input  [7:0] B,
  input  clk,
  output [7:0] out_4
);

  wire alu_1_eq, alu_1_gt, alu_1_lt, alu_1_of;
  wire [7:0] alu_1_r;

  ALU alu_1 (.Op(in_1), .A(A), .B(B), .OF(alu_1_of), .eq(alu_1_eq), .lt(alu_1_lt), .gt(alu_1_gt), .R(alu_1_r));
  LED led_1 (.in(alu_1_of));
  LED led_2 (.in(alu_1_eq));
  LED led_3 (.in(alu_1_lt));
  LED led_4 (.in(alu_1_gt));
  Seven_Seg_Hex seven_seg_hex_1 (.d(out_4[3:0]), .dp(1'b1));
  Register #(.Bits(8)) register_1 (.D(alu_1_r), .C(clk), .en(1'b1), .Q(out_4));
  Seven_Seg_Hex seven_seg_hex_2 (.d(out_4[7:4]), .dp(1'b1));

  // Notes on the sheet:
  //   clk: Hz: 5
endmodule
