// Digital circuit comparador.dig as structural Verilog
module comparador (
  input  [7:0] A,
  input  [7:0] B,
  output eq,
  output lt,
  output gt
);

  wire comparador1bit_1_p4, comparador1bit_1_p5, comparador1bit_1_p6, comparador1bit_2_p4,
       comparador1bit_2_p5, comparador1bit_2_p6, comparador1bit_3_p4, comparador1bit_3_p5,
       comparador1bit_3_p6, comparador1bit_4_p4, comparador1bit_4_p5, comparador1bit_4_p6,
       comparador1bit_5_p4, comparador1bit_5_p5, comparador1bit_5_p6, comparador1bit_6_p4,
       comparador1bit_6_p5, comparador1bit_6_p6, comparador1bit_7_p4, comparador1bit_7_p5,
       comparador1bit_7_p6, comparador1bit_8_p5, comparador1bit_8_p6;

  // comparador1bit comparador1bit_1: pin names not known; wires that end beside it: 1'b1, A[7], B[7], comparador1bit_1_p4, comparador1bit_1_p5, comparador1bit_1_p6
  // comparador1bit comparador1bit_2: pin names not known; wires that end beside it: comparador1bit_1_p4, A[6], B[6], comparador1bit_2_p4, comparador1bit_2_p5, comparador1bit_2_p6
  // comparador1bit comparador1bit_3: pin names not known; wires that end beside it: comparador1bit_2_p4, A[5], B[5], comparador1bit_3_p4, comparador1bit_3_p5, comparador1bit_3_p6
  // comparador1bit comparador1bit_4: pin names not known; wires that end beside it: comparador1bit_3_p4, A[4], B[4], comparador1bit_4_p4, comparador1bit_4_p5, comparador1bit_4_p6
  // comparador1bit comparador1bit_5: pin names not known; wires that end beside it: comparador1bit_4_p4, A[3], B[3], comparador1bit_5_p4, comparador1bit_5_p5, comparador1bit_5_p6
  // comparador1bit comparador1bit_6: pin names not known; wires that end beside it: comparador1bit_5_p4, A[2], B[2], comparador1bit_6_p4, comparador1bit_6_p5, comparador1bit_6_p6
  xor xor_1 (lt, comparador1bit_8_p6, comparador1bit_7_p6, comparador1bit_6_p6, comparador1bit_5_p6, comparador1bit_4_p6, comparador1bit_3_p6, comparador1bit_2_p6, comparador1bit_1_p6);
  // comparador1bit comparador1bit_7: pin names not known; wires that end beside it: comparador1bit_6_p4, A[1], B[1], comparador1bit_7_p4, comparador1bit_7_p5, comparador1bit_7_p6
  // comparador1bit comparador1bit_8: pin names not known; wires that end beside it: comparador1bit_7_p4, A[0], B[0], eq, comparador1bit_8_p5, comparador1bit_8_p6
  xor xor_2 (gt, comparador1bit_8_p5, comparador1bit_7_p5, comparador1bit_6_p5, comparador1bit_5_p5, comparador1bit_4_p5, comparador1bit_3_p5, comparador1bit_2_p5, comparador1bit_1_p5);
endmodule
