// Digital circuit fullAdder.dig as structural Verilog
module fullAdder (
  input  Cin,
  input  A,
  input  B,
  output Soma,
  output Cout
);

  wire halfadder_1_c, halfadder_1_s, halfadder_2_c;

  halfAdder halfadder_1 (.A(A), .B(B), .S(halfadder_1_s), .C(halfadder_1_c));
  halfAdder halfadder_2 (.A(Cin), .B(halfadder_1_s), .S(Soma), .C(halfadder_2_c));
  or or_1 (Cout, halfadder_2_c, halfadder_1_c);
endmodule
