// Digital circuit fullAdder16.dig as structural Verilog
module fullAdder16 (
  input  [7:0] A,
  input  [7:0] B,
  input  Cin,
  output Cout,
  output [7:0] Soma
);

  wire fulladder_1_cout, fulladder_2_cout, fulladder_3_cout, fulladder_4_cout, fulladder_5_cout,
       fulladder_6_cout, fulladder_7_cout;

  fullAdder fulladder_1 (.Cin(Cin), .A(A[0]), .B(B[0]), .Soma(Soma[0]), .Cout(fulladder_1_cout));
  fullAdder fulladder_2 (.Cin(fulladder_1_cout), .A(A[1]), .B(B[1]), .Soma(Soma[1]), .Cout(fulladder_2_cout));
  fullAdder fulladder_3 (.Cin(fulladder_2_cout), .A(A[2]), .B(B[2]), .Soma(Soma[2]), .Cout(fulladder_3_cout));
  fullAdder fulladder_4 (.Cin(fulladder_3_cout), .A(A[3]), .B(B[3]), .Soma(Soma[3]), .Cout(fulladder_4_cout));
  fullAdder fulladder_5 (.Cin(fulladder_4_cout), .A(A[4]), .B(B[4]), .Soma(Soma[4]), .Cout(fulladder_5_cout));
  fullAdder fulladder_6 (.Cin(fulladder_5_cout), .A(A[5]), .B(B[5]), .Soma(Soma[5]), .Cout(fulladder_6_cout));
  fullAdder fulladder_7 (.Cin(fulladder_6_cout), .A(A[6]), .B(B[6]), .Soma(Soma[6]), .Cout(fulladder_7_cout));
  fullAdder fulladder_8 (.Cin(fulladder_7_cout), .A(A[7]), .B(B[7]), .Soma(Soma[7]), .Cout(Cout));
endmodule
