// Digital circuit multiplicador.dig as structural Verilog
module multiplicador (
  input  [3:0] A,
  input  [3:0] B,
  output [7:0] R,
  output Cout
);

  wire fulladder16_1_cout, fulladder16_2_cout;
  wire [3:0] seletor_1_is, seletor_2_is, seletor_3_is, seletor_4_is;
  wire [7:0] fulladder16_1_soma, fulladder16_2_soma, leftshift_1_als, leftshift_2_als, leftshift_3_als,
       leftshift_4_als, leftshift_5_als, leftshift_6_als;

  seletor seletor_1 (.I(A), .S(B[0]), .IS(seletor_1_is));
  seletor seletor_2 (.I(A), .S(B[1]), .IS(seletor_2_is));
  seletor seletor_3 (.I(A), .S(B[2]), .IS(seletor_3_is));
  seletor seletor_4 (.I(A), .S(B[3]), .IS(seletor_4_is));
  leftShift leftshift_1 (.A({4'b0000, seletor_2_is}), .ALs(leftshift_1_als));
  leftShift leftshift_2 (.A({4'b0000, seletor_3_is}), .ALs(leftshift_2_als));
  leftShift leftshift_3 (.A({4'b0000, seletor_4_is}), .ALs(leftshift_3_als));
  leftShift leftshift_4 (.A(leftshift_2_als), .ALs(leftshift_4_als));
  leftShift leftshift_5 (.A(leftshift_3_als), .ALs(leftshift_5_als));
  fullAdder16 fulladder16_1 (
    .A({4'b0000, seletor_1_is}), .B(leftshift_1_als), .Cin(1'b0), .Cout(fulladder16_1_cout),
    .Soma(fulladder16_1_soma));
  leftShift leftshift_6 (.A(leftshift_5_als), .ALs(leftshift_6_als));
  fullAdder16 fulladder16_2 (
    .A(fulladder16_1_soma), .B(leftshift_4_als), .Cin(fulladder16_1_cout), .Cout(fulladder16_2_cout),
    .Soma(fulladder16_2_soma));
  fullAdder16 fulladder16_3 (
    .A(fulladder16_2_soma), .B(leftshift_6_als), .Cin(fulladder16_2_cout), .Cout(Cout), .Soma(R));
  // Pins of 1 and 4 bits meet at B
endmodule
