// Digital circuit seletor.dig as structural Verilog
module seletor (
  input  [3:0] I,
  input  S,
  output [3:0] IS
);

  and and_1 (IS[0], S, I[0]);
  and and_2 (IS[1], S, I[1]);
  and and_3 (IS[2], S, I[2]);
  and and_4 (IS[3], S, I[3]);

  // Other names for the same wires on the sheet: Es = S
endmodule
