// Digital circuit seletor8bit.dig as structural Verilog
module seletor8bit (
  input  [7:0] N,
  input  S,
  output [7:0] NS
);

  and and_1 (NS[0], S, N[0]);
  and and_2 (NS[1], S, N[1]);
  and and_3 (NS[2], S, N[2]);
  and and_4 (NS[3], S, N[3]);
  and and_5 (NS[4], S, N[4]);
  and and_6 (NS[5], S, N[5]);
  and and_7 (NS[6], S, N[6]);
  and and_8 (NS[7], S, N[7]);

  // Other names for the same wires on the sheet: Es = S
endmodule
