// Digital circuit subtrator8.dig as structural Verilog
module subtrator8 (
  input  [7:0] B,
  input  [7:0] A,
  output Cout,
  output [7:0] Diff
);

  wire [7:0] not_1_out;

  assign not_1_out = ~B;  // Not not_1, 8 bits wide
  fullAdder16 fulladder16_1 (.A(A), .B(not_1_out), .Cin(1'b1), .Cout(Cout), .Soma(Diff));
endmodule
